// Logisim project co.circ as structural Verilog: 3 circuits, main circuit main
module main (
  input  in_1,
  output out_2
);

  wire CLOCK, D_FLIP_FLOP_q, LOAD_AC, LOAD_AR, LOAD_DR, LOAD_IR, LOAD_PC, MEMORY_READ, MEMORY_WRITE,
       not_1_out, PC_INC, r, SC_CLEAR, T0, T1, T2, T3, T4, T5, T6, T7;
  wire [2:0] ALU, control_unit_1_bus_selection;
  wire [3:0] COUNTER_q;
  wire [6:0] AR_q, bit_extender_1_out, bit_extender_2_out, PC_q;
  wire [15:0] AC, alu_1_ac_output, bit_extender_3_out, bit_extender_4_out, DR_q, IR, multiplexer_1_out,
       ram_1_data, TR_q;

  Clock u_CLOCK (.out(CLOCK));
  Control_unit control_unit_1 (
    .IR(IR), .AC(AC), .T0(T0), .T1(T1), .T2(T2), .T3(T3), .T4(T4), .T5(T5), .T6(T6), .T7(T7),
    .LOAD_AR(LOAD_AR), .MEORY_WRITE(MEMORY_WRITE), .LOAD_DR(LOAD_DR), .LOAD_AC(LOAD_AC), .ALU(ALU),
    .PC_INC(PC_INC), .LOAD_IR(LOAD_IR), .BUS_SELECTION(control_unit_1_bus_selection),
    .MEMORY_READ(MEMORY_READ), .r(r), .SC_CLEAR(SC_CLEAR), .LD_PC(LOAD_PC));
  Decoder #(.select(4), .enable("false")) decoder_1 (
    .out0(T0), .out1(T1), .out2(T2), .out3(T3), .out4(T4), .out5(T5), .out6(T6), .out7(T7), .sel(COUNTER_q));  // open: out8, out9, out10, out11, out12, out13, out14, out15
  not not_1 (not_1_out, SC_CLEAR);
  Bit_Extender #(.in_width(16), .out_width(7)) bit_extender_1 (.in(multiplexer_1_out), .out(bit_extender_1_out));
  Counter #(.width(4), .max('hf)) COUNTER (
    .load(1'b0), .count(not_1_out), .Q(COUNTER_q), .clk(CLOCK), .clr(D_FLIP_FLOP_q));  // open: D, carry
  D_Flip_Flop D_FLIP_FLOP (.clk(CLOCK), .D(SC_CLEAR), .Q(D_FLIP_FLOP_q));  // open: Qn, preset, en, reset
  Bit_Extender #(.in_width(16), .out_width(7)) bit_extender_2 (.in(multiplexer_1_out), .out(bit_extender_2_out));
  Register #(.width(7)) AR (.D(bit_extender_2_out), .en(LOAD_AR), .Q(AR_q), .clk(CLOCK));  // open: clr
  Register #(.width(16)) TR (.D(multiplexer_1_out), .en(in_1), .Q(TR_q), .clk(CLOCK));  // open: clr
  Register #(.width(16)) DR (.D(multiplexer_1_out), .en(LOAD_DR), .Q(DR_q), .clk(CLOCK));  // open: clr
  Register #(.width(16)) u_AC (.D(alu_1_ac_output), .en(LOAD_AC), .Q(AC), .clk(CLOCK));  // open: clr
  Counter #(.width(7), .max('h7f)) PC (
    .load(LOAD_PC), .D(bit_extender_1_out), .count(PC_INC), .Q(PC_q), .clk(CLOCK));  // open: carry, clr
  Register #(.width(16)) u_IR (.D(multiplexer_1_out), .en(LOAD_IR), .Q(IR), .clk(CLOCK));  // open: clr
  RAM #(.addrWidth(7), .dataWidth(16), .bus("separate")) ram_1 (
    .addr(AR_q), .din(multiplexer_1_out), .data(ram_1_data), .str(MEMORY_WRITE), .clk(CLOCK), .ld(MEMORY_READ));  // open: sel, clr
  assign bit_extender_3_out = {{9{1'b0}}, AR_q};  // Bit_Extender bit_extender_3
  ALU alu_1 (.A(DR_q), .B(AC), .in_3(ALU), .E(out_2), .AC_Output(alu_1_ac_output));
  assign bit_extender_4_out = {{9{1'b0}}, PC_q};  // Bit_Extender bit_extender_4
  Multiplexer #(.select(3), .width(16)) multiplexer_1 (
    .in0(ram_1_data), .in1(bit_extender_3_out), .in2(TR_q), .in3(DR_q), .in4(AC), .in5(bit_extender_4_out),
    .in6(IR), .out(multiplexer_1_out), .sel(control_unit_1_bus_selection));  // open: in7, en
endmodule

module ALU (
  input  [15:0] A,
  input  [15:0] B,
  input  [2:0] in_3,
  output E,
  output [15:0] AC_Output
);

  wire adder_1_cout, adder_2_cout, subtractor_1_bout;
  wire [15:0] adder_1_out, adder_2_out, and_1_out, or_1_out, subtractor_1_out, xor_1_out;

  Adder #(.width(16)) adder_1 (.a(A), .b(B), .out(adder_1_out), .cin(1'b0), .cout(adder_1_cout));
  Subtractor #(.width(16)) subtractor_1 (.a(A), .b(B), .out(subtractor_1_out), .bin(1'b0), .bout(subtractor_1_bout));
  assign and_1_out = A & B;  // AND_Gate and_1, 16 bits wide
  assign or_1_out = A | B;  // OR_Gate or_1, 16 bits wide
  assign xor_1_out = A ^ B;  // XOR_Gate xor_1, 16 bits wide
  Adder #(.width(16)) adder_2 (.a(A), .b({16{1'b0}}), .out(adder_2_out), .cin(1'b1), .cout(adder_2_cout));
  or or_2 (E, adder_1_cout, subtractor_1_bout, adder_2_cout);
  Multiplexer #(.select(3), .width(16)) multiplexer_1 (
    .in1(adder_1_out), .in2(subtractor_1_out), .in3(A), .in4(and_1_out), .in5(or_1_out), .in6(xor_1_out),
    .in7(adder_2_out), .out(AC_Output), .sel(in_3));  // open: in0, en
endmodule

// CONTROL UNIT
module Control_unit (
  input  [15:0] IR,
  input  [15:0] AC,
  input  T0,
  input  T1,
  input  T2,
  input  T3,
  input  T4,
  input  T5,
  input  T6,
  input  T7,
  output LOAD_AR,
  output MEORY_WRITE,
  output LOAD_DR,
  output LOAD_AC,
  output [2:0] ALU,
  output PC_INC,
  output LOAD_IR,
  output [2:0] BUS_SELECTION,
  output MEMORY_READ,
  output r,
  output SC_CLEAR,
  output LD_PC
);

  wire and_1_out, and_2_out, and_3_out, and_4_out, and_5_out, and_6_out, and_7_out, and_8_out, and_9_out,
       and_10_out, and_11_out, and_12_out, and_14_out, and_15_out, and_16_out, and_17_out, and_18_out,
       and_19_out, and_20_out, and_21_out, and_22_out, and_23_out, and_24_out, and_25_out, and_26_out,
       and_27_out, and_28_out, and_29_out, and_30_out, and_31_out, and_32_out, and_33_out, and_35_out,
       and_36_out, and_37_out, and_38_out, D0, D1, D2, D3, D4, D5, D6, D7, nor_1_out, or_1_out, or_2_out,
       or_3_out, or_4_out;

  Decoder #(.select(3), .enable("false")) decoder_1 (
    .out0(D0), .out1(D1), .out2(D2), .out3(D3), .out4(D4), .out5(D5), .out6(D6), .out7(D7), .sel(IR[14:12]));
  and and_1 (and_1_out, D1, T5);
  and and_2 (and_2_out, D5, T5);
  and and_3 (and_3_out, D5, T6);
  and and_4 (and_4_out, T5, D0);
  or u_LOAD_AR (LOAD_AR, T0, T2);
  and and_5 (and_5_out, T5, D2);
  and and_6 (and_6_out, D7, IR[5], T4);
  and and_7 (and_7_out, D7, T4, IR[5]);
  and and_8 (and_8_out, D5, T5);
  and and_9 (and_9_out, D2, T5);
  or u_LOAD_AC (LOAD_AC, and_5_out, and_6_out, and_1_out, and_2_out, and_3_out, and_4_out);
  and and_10 (and_10_out, D1, T5);
  and and_11 (and_11_out, D5, T6);
  or or_1 (or_1_out, and_8_out, and_9_out);
  and and_12 (and_12_out, D0, T5);
  Priority_Encoder priority_encoder_1 (
    .in0(1'b0), .in1(and_10_out), .in2(and_11_out), .in3(or_1_out), .in4(and_12_out), .in5(1'b0), .in6(1'b0),
    .in7(and_7_out), .out(ALU));  // open: en_in, gs, en_out
  and and_13 (MEORY_WRITE, D3, T4);
  or or_2 (or_2_out, D0, D1, D2, D5);
  and and_14 (and_14_out, T4, or_2_out);
  or u_MEMORY_READ (MEMORY_READ, and_14_out, T1);
  and and_15 (and_15_out, D0, T4);
  and and_16 (and_16_out, D2, T4);
  and and_17 (and_17_out, D1, T4);
  and and_18 (and_18_out, D5, T4);
  and and_19 (and_19_out, D5, T5);
  and and_20 (and_20_out, r, IR[5]);
  and and_21 (and_21_out, D5, T4);
  and and_22 (and_22_out, D1, T4);
  and and_23 (and_23_out, D0, T4);
  and and_24 (and_24_out, D2, T4);
  or or_3 (or_3_out, T1, and_21_out, and_22_out, and_23_out, and_24_out);
  and and_25 (and_25_out, D4, T4);
  and and_26 (and_26_out, D5, T5);
  and and_27 (and_27_out, D3, T4);
  and and_28 (and_28_out, r, IR[5]);
  or u_LOAD_DR (LOAD_DR, and_15_out, and_16_out, and_17_out, and_18_out, and_19_out, and_20_out);
  or or_4 (or_4_out, and_26_out, and_27_out, and_28_out);
  and and_29 (and_29_out, T4, D4);
  nor nor_1 (nor_1_out, AC[0], AC[1], AC[2], AC[3], AC[4], AC[5], AC[6], AC[7], AC[8], AC[9], AC[10], AC[11], AC[12], AC[13], AC[14], AC[15]);
  and and_30 (and_30_out, r, nor_1_out, IR[2]);
  Priority_Encoder priority_encoder_2 (
    .in0(or_3_out), .in1(and_25_out), .in2(1'b0), .in3(1'b0), .in4(or_4_out), .in5(T0), .in6(T2), .in7(1'b0),
    .out(BUS_SELECTION));  // open: en_in, gs, en_out
  and and_31 (and_31_out, r, IR[2]);
  and and_32 (and_32_out, T5, D1);
  and and_33 (and_33_out, T4, D3);
  and and_34 (r, D7, T3);
  or u_PC_INC (PC_INC, T1, and_30_out);
  and and_35 (and_35_out, D7, T4, IR[5]);
  and and_36 (and_36_out, T6, D5);
  and and_37 (and_37_out, D2, T5);
  and and_38 (and_38_out, T5, D0);
  or u_SC_CLEAR (SC_CLEAR, and_31_out, and_35_out, and_36_out, and_32_out, and_29_out, and_33_out, and_37_out, and_38_out);
  and and_39 (LD_PC, D4, T4);

  assign LOAD_IR = T1;

  // Other names for the same wires on the sheet: B0 = IR[0]; B1 = IR[1]; B2 = IR[2]; B3 = IR[3]; B4 = IR[4];
  //   B5 = IR[5]; B6 = IR[6]; B7 = IR[7]; B8 = IR[8]; B9 = IR[9]; B10 = IR[10]; B11 = IR[11]; I = IR[15]
endmodule
